# Fritzing sketch design (saved by Fritzing 0.9.9b)
breadboards: 1

parts:
  Mod1 = Raspberry Pi 4B
  Mod2 = Raspberry Pi Pico
  M1 = fc-51 [package=THT]
  M2 = fc-51 [package=THT]
  M3 = fc-51 [package=THT]
  M4 = fc-51 [package=THT]
  R1 = Resistor [tolerance=±5% resistance=220 package="0603 [SMD]"]
  R2 = Resistor [tolerance=±5% resistance=220 package="0603 [SMD]"]
  R3 = Resistor [tolerance=±5% resistance=220 package="0603 [SMD]"]
  R4 = Resistor [tolerance=±5% resistance=220 package="0603 [SMD]"]
  R5 = Resistor [tolerance=±5% resistance=220 package="0603 [SMD]"]
  R6 = Resistor [tolerance=±5% resistance=220 package="0603 [SMD]"]
  R7 = Resistor [tolerance=±5% resistance=220 package="0603 [SMD]"]
  J1 = Power Jack [package=power_jack_smd]
  S1 = H-Bridge with L298N
  J2 = Power Jack [package=power_jack_smd]

nets:
  N1: Mod1.5V, M1.pin3, M2.pin3, M3.pin3, M4.pin3
  GND: Mod1.GPIO3, Mod1.GND, Mod2.pin_23, Mod2.pin_38, Mod2.pin_42, M1.pin2, M2.pin2, M3.pin2, M4.pin2, J1.GND, S1.GND, J2.GND
  N2: Mod1.GPIO17, Mod2.pin_27, R5.Pin_0, R5.Pin_1
  N3: Mod1.GPIO27, Mod2.pin_25, R6.Pin_0, R6.Pin_1
  N4: Mod1.GPIO22, Mod2.pin_24, R7.Pin_0, R7.Pin_1
  N5: Mod1.GPIO5, M1.pin1, R1.Pin_0, R1.Pin_1
  N6: Mod1.GPIO6, M2.pin1, R2.Pin_0, R2.Pin_1
  N7: Mod1.GPIO13, M3.pin1, R3.Pin_0, R3.Pin_1
  N8: Mod1.GPIO19, M4.pin1, R4.Pin_0, R4.Pin_1
  N9: Mod1.GPIO26, J1.GNDBREAK
  N10: Mod2.pin_10, S1.ENA
  N11: Mod2.pin_11, S1.IN1
  N12: Mod2.pin_12, S1.IN2
  N13: Mod2.pin_39, S1.5V
  N14: S1.12V, J2.GNDBREAK

notes:
  To Train

custom parts:
  Raspberry Pi Pico: Raspberry Pi Pico. Based around the RP2040 microcontroller the Pico is a low cost microcontroller device bringing Raspberry Pi quality, cost, and easy of use to the microcontroller space. Jan 2021, Split part in to two versions: tht (this one) and SMD. This one will drill holes for a .1 in header in pcb to allow plugging in the module as well as providing pads to solder the module to the top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
  H-Bridge with L298N: h-bridge
